# Fritzing sketch shema (saved by Fritzing 0.9.3b)

parts:
  Part1 = LIDAR-Lite
  Part2 = Arduino Mega 2560 (Rev3)
  R1 = Resistor [tolerance=±5% resistance=01k package="0603 [SMD]"]
  J1 = Basic Servo

nets:
  5V: Part1.5V, Part2.5V
  N1: Part1.MODE, Part2.D7_PWM, R1.Pin_0
  GND: Part1.GND, Part2.GND
  N2: Part2.D9_PWM, J1.pulse
  N3: Part2.D2_PWM, R1.Pin_1

custom parts:
  LIDAR-Lite: PulsedLight LIDAR-Lite Sensor
